// Logisim project processor.circ as structural Verilog: 11 circuits, main circuit IFstage
module IFstage (
  input  in_1,
  input  [31:0] in_2,
  input  in_3,
  input  in_4,
  input  in_5,
  input  in_6,
  output [31:0] out_7,
  output [31:0] out_8
);

  wire not_1_out;
  wire [31:0] multiplexer_1_out, PC_q, vhdl_entity_1_p3;

  Register #(.width(32)) PC (.D(multiplexer_1_out), .en(not_1_out), .clk(in_1), .Q(PC_q), .clr(in_6));
  not not_1 (not_1_out, in_5);
  Multiplexer #(.width(32), .enable("false")) multiplexer_1 (
    .in0(in_2), .in1(out_7), .out(multiplexer_1_out), .sel(in_3));
  Adder #(.width(32)) adder_1 (.a(32'h4), .b(PC_q), .out(out_7));  // open: cin, cout
  // VHDL_Entity #(.content("library ieee;\nuse ieee.std_logic_1164.all;\nuse ieee.std_logic_textio.all;\nuse ieee.numeric_std.all;\nuse std.textio.all;\n\nentity imem is\n	port(\n		a  : in  std_logic_vector(31 downto 0);\n		rd : out std_logic_vector(31 downto 0)\n	);\nend imem;\n\narchitecture RTL of imem is\n	type memoryArray is array (127 downto 0) of std_logic_vector(31 downto 0);\n	impure function init_rom return memoryArray is\n		file inputText     : text;\n		variable inputLine : line;\n		variable temporal  : std_logic_vector(31 downto 0);\n		variable rom       : memoryArray := (others => (others => '0'));\n	begin\n		file_open(inputText, \"instr_memfile.dat\", read_mode);\n		for index in 0 to 127 loop\n			if (endfile(inputText)) then\n				exit;\n			else\n				readline(inputText, inputLine);\n				hread(inputLine, temporal);\n				rom(index) := temporal;\n			end if;\n		end loop;\n		file_close(inputText);\n		return rom;\n	end init_rom;\n	signal rom : memoryArray := init_rom;\nbegin\n	rd <= rom(to_integer(unsigned(a(8 downto 2)))) after 50 ns;\nend RTL;")) vhdl_entity_1: pin names not known; wires that end beside it: not_1_out, PC_q, vhdl_entity_1_p3
  Multiplexer #(.width(32), .enable("false")) multiplexer_2 (
    .in0({32{1'b0}}), .in1(vhdl_entity_1_p3), .out(out_8), .sel(in_4));
endmodule

module IFIDpipe (
  input  in_1,
  input  [31:0] in_2,
  input  [31:0] in_3,
  input  in_4,
  input  in_5,
  output [31:0] out_6,
  output [31:0] out_7
);

  Register #(.width(32)) register_1 (.D(in_2), .en(in_4), .clk(in_1), .Q(out_6), .clr(in_5));
  Register #(.width(32)) register_2 (.D(in_3), .en(in_4), .clk(in_1), .Q(out_7), .clr(in_5));
endmodule

module IDstage (
  input  in_1,
  input  [31:0] in_2,
  input  [31:0] in_3,
  input  [31:0] in_4,
  input  [4:0] in_5,
  input  in_6,
  input  in_7,
  input  [4:0] in_8,
  input  in_9,
  input  in_10,
  input  [4:0] in_11,
  input  in_12,
  input  [31:0] in_13,
  output [31:0] out_14,
  output [31:0] out_15,
  output [31:0] out_16,
  output [31:0] out_17,
  output [2:0] out_18,
  output out_19,
  output [1:0] out_20,
  output [1:0] out_21,
  output out_22,
  output out_23,
  output out_24,
  output out_25,
  output [4:0] out_26,
  output out_27,
  output out_28,
  output out_29,
  output out_30
);

  wire comparator_1_eq, not_1_out, vhdl_entity_1_p3, vhdl_entity_1_p4, vhdl_entity_1_p5, vhdl_entity_1_p7,
       vhdl_entity_1_p8, vhdl_entity_1_p9, vhdl_entity_1_p11, vhdl_entity_1_p12, vhdl_entity_1_p14,
       vhdl_entity_2_p7, vhdl_entity_2_p19, vhdl_entity_2_p20;
  wire [27:0] bit_extender_1_out, shifter_1_out;
  wire [31:0] adder_1_out, bit_extender_2_out, bit_extender_3_out, multiplexer_4_out, multiplexer_5_out,
       shifter_2_out;

  assign bit_extender_1_out = {{2{1'b0}}, in_3[25:0]};  // Bit_Extender bit_extender_1
  Shifter #(.width(28)) shifter_1 (.in(bit_extender_1_out), .\dist (5'b00010), .out(shifter_1_out));
  // VHDL_Entity #(.content("library ieee;\nuse ieee.std_logic_1164.all;\nuse ieee.numeric_std.all;\n\nentity maindec is\n	port(\n		op       : in  std_logic_vector(5 downto 0); -- Op Code Field of Instruction.\n		funct    : in  std_logic_vector(5 downto 0); -- Funct Field of R-type Instructions.\n		branch   : out std_logic;\n		jump     : out std_logic;\n		lui      : out std_logic;\n		isLoad   : out std_logic;\n		isStore  : out std_logic;\n		isNop    : out std_logic; -- This is all 0s, as sll $zero, $zero, $zero.\n		readsRs  : out std_logic; -- The Instruction reads the 1st source register (rs).\n		readsRt  : out std_logic; -- The Instruction reads the 2nd source register (rt).\n		memwrite : out std_logic;\n		regwrite : out std_logic;\n		memtoreg : out std_logic;\n		regdst   : out std_logic;\n		aluctrl  : out std_logic_vector(2 downto 0);\n		alusrc   : out std_logic\n	);\nend maindec;\n\narchitecture RTL of maindec is\n	-- Implemented Instructions:\n	-- lw, sw,\n	-- beq, j,\n	-- addi, addiu (same as addi, ignores overflows),\n	-- ori,\n	-- lui,\n	-- add, sub, and, or, slt.\nbegin\n	proc : process(op, funct)\n	begin\n		-- Default Values for Signals.\n		branch   <= '0';\n		jump     <= '0';\n		lui      <= '0';\n		isLoad   <= '0';\n		isStore  <= '0';\n		isNop    <= '0';\n		readsRs  <= '1'; -- Most Instructions read the rs register.\n		readsRt  <= '0';\n		memwrite <= '0'; -- Don't write to the Data Memory.\n		regwrite <= '0'; -- Don't write result to the Register File.\n		memtoreg <= 'X'; -- Result Mux, unimportant.\n		regdst   <= '0'; -- Destination Register, unimportant, but set to 0 for simplicity.\n		aluctrl  <= \"XXX\"; -- ALU operation, unimportant.\n		alusrc   <= 'X'; -- Second ALU source, unimportant.\n		case op is\n			when \"000000\" =>            -- RTYPE --\n				regwrite <= '1'; -- All Implemented R-type instructions store result.\n				regdst   <= '1'; -- Rd is the Destination Register.\n				memtoreg <= '0'; -- AluOut to be stored to the Register File.\n				alusrc   <= '0'; -- Second ALU source is the register value.\n				readsRt  <= '1';\n				case funct is\n					when \"100000\" =>    -- ADD --\n						aluctrl <= \"010\";\n					when \"100010\" =>    -- SUB --\n						aluctrl <= \"110\";\n					when \"100100\" =>    -- AND --\n						aluctrl <= \"000\";\n					when \"100101\" =>    -- OR  --\n						aluctrl <= \"001\";\n					when \"101010\" =>    -- SLT --\n						aluctrl <= \"111\";\n					when \"000000\" =>    -- SLL --\n						isNop    <= '1'; -- Assuming NOP, even if rs, rt, and rd are not $zero.\n						regwrite <= '0';\n					when others =>    -- Unknown.\n						aluctrl <= \"XXX\";\n				end case;\n			when \"100011\" =>            --  LW   --\n				isLoad   <= '1';\n				regwrite <= '1'; -- Write Result to Register File.\n				regdst   <= '0'; -- Rt is the Destination Register.\n				memtoreg <= '1'; -- Signal Result is Mem Output.\n				alusrc   <= '1'; -- Second ALU source is Immediate.\n				aluctrl  <= \"010\";\n			when \"101011\" =>            --  SW   --\n				isStore  <= '1';\n				memwrite <= '1'; -- Write to Data Memory.\n				alusrc   <= '1'; -- Second ALU  source is Immediate.\n				aluctrl  <= \"010\";\n				readsRt  <= '1';\n			when \"000100\" =>            --  BEQ  --\n				branch  <= '1';\n				readsRt <= '1';\n			when \"001000\" | \"001001\" => -- ADDI, ADDIU --\n				regwrite <= '1'; -- Write Result to Register File.\n				regdst   <= '0'; -- Rt is the Destination Register.\n				memtoreg <= '0'; -- Signal Result is ALU Output.\n				alusrc   <= '1'; -- Second ALU source is Immediate.\n				aluctrl  <= \"010\";\n			when \"000010\" =>            --   J   --\n				jump    <= '1';\n				readsRs <= '0'; -- Does not read Rs.\n			when \"001111\" =>            --  LUI  --\n				lui      <= '1';\n				regwrite <= '1'; -- Write Result to Register File.\n				regdst   <= '0'; -- Rt is the Destination Register.\n				memtoreg <= '0'; -- Signal Result is ALU Output.\n				alusrc   <= '1'; -- Second ALU Source is Immediate.\n				readsRs  <= '0'; -- Does not read Rs.\n				aluctrl  <= \"001\";\n			when \"001101\" =>            --  ORI  --\n				regwrite <= '1'; -- Write Result to Register File.\n				regdst   <= '0'; -- Rt is the Destination Register.\n				memtoreg <= '0'; -- Signal Result is ALU Output.\n				alusrc   <= '1'; -- Second ALU Source is Immediate.\n				aluctrl  <= \"001\";\n			when others =>            -- Unknown --\n				isNop <= 'X'; -- Default values at the top cover this case.\n		end case;\n	end process proc;\nend RTL;")) vhdl_entity_1: pin names not known; wires that end beside it: in_3[31:26], in_3[5:0], vhdl_entity_1_p3, vhdl_entity_1_p4, vhdl_entity_1_p5, out_22, vhdl_entity_1_p7, vhdl_entity_1_p8, vhdl_entity_1_p9, vhdl_entity_1_p9, vhdl_entity_1_p11, vhdl_entity_1_p12, out_25, vhdl_entity_1_p14, out_18, out_19
  assign bit_extender_2_out = {{16{in_3[15]}}, in_3[15:0]};  // Bit_Extender bit_extender_2
  assign bit_extender_3_out = {{16{in_3[15]}}, in_3[15:0]};  // Bit_Extender bit_extender_3
  Multiplexer #(.width(5), .enable("false")) multiplexer_1 (
    .in0(in_3[20:16]), .in1(in_3[15:11]), .sel(vhdl_entity_1_p14));  // open: out
  Shifter #(.width(32)) shifter_2 (.in(bit_extender_2_out), .\dist (5'b00010), .out(shifter_2_out));
  Multiplexer #(.width(32), .enable("false")) multiplexer_2 (
    .in0(bit_extender_2_out), .in1(bit_extender_3_out), .out(out_17), .sel(vhdl_entity_1_p5));
  Adder #(.width(32)) adder_1 (.a(in_2), .b(shifter_2_out), .out(adder_1_out));  // open: cin, cout
  // VHDL_Entity #(.content("library ieee;\nuse ieee.std_logic_1164.all;\nuse ieee.numeric_std.all;\n\nentity pipe_ctrl is\n	port(\n		rs            : in  std_logic_vector(4 downto 0);\n		rt            : in  std_logic_vector(4 downto 0);\n		isStore       : in  std_logic;\n		isNop         : in  std_logic;\n		readsRs       : in  std_logic;\n		readsRt       : in  std_logic;\n		branch        : in  std_logic;\n		jump          : in  std_logic;\n		brTaken       : in  std_logic;\n		-- From Stage Ex  --\n		ex_rd         : in  std_logic_vector(4 downto 0);\n		ex_regWrite   : in  std_logic;\n		ex_isLoad     : in  std_logic;\n		-- From Stage Mem --\n		mem_rd        : in  std_logic_vector(4 downto 0);\n		mem_regWrite  : in  std_logic;\n		mem_isLoad    : in  std_logic;\n		--  For Stage IF  --\n		flush         : out std_logic;\n		flowChange    : out std_logic;\n		stall         : out std_logic;\n		--  For Stage ID  --\n		id_forwardA   : out std_logic_vector(1 downto 0) := \"00\"; -- Select Register from Register File.\n		id_forwardB   : out std_logic_vector(1 downto 0) := \"00\"; -- Select Register from Register File.\n		id_eqFwdA     : out std_logic := '0';\n		id_eqFwdB     : out std_logic := '0';\n		id_ldstBypass : out std_logic := '0'\n	);\nend  pipe_ctrl;\n\narchitecture RTL of pipe_ctrl is\n	signal ofStall : std_logic;\n	constant empty : std_logic_vector(4 downto 0) := (others => '0');\nbegin\n	stall         <= ofStall;\n	flush         <= (branch and brTaken and not ofStall) or jump;\n	flowChange    <= (branch and brTaken and not ofStall) or jump;\n	-- Forwarding Control for Operand A (rs):\n	-- 00 -- From Register File.\n	-- 01 -- From Stage Mem to Stage Ex.\n	-- 10 -- From Stage Wb to Stage Ex.\n	id_forwardA <= \"10\" when ((ex_regWrite = '1')	-- Valid Instruction producing Result at Stage Ex.\n						  and (ex_rd = rs)			-- Ex Target is our Rs source.\n						  and (readsRs = '1')		-- This is not a Jump Instruction, Rs is read from.\n						  and (rs /= empty)) else	-- Not reading $zero.\n				   \"01\" when ((mem_regWrite = '1')	-- Valid Instruction producing Result at Stage Mem.\n				   	      and (mem_rd = rs)			-- Mem Target is our Rs source.\n				   	      and (readsRs = '1')		-- This is not a Jump Instruction, Rs is read from.\n				   	      and (rs /= empty)) else	-- Not reading $zero.\n				   \"00\";\n	-- Forwarding Control for Operand B (rt):\n	-- It is only needed for R-type Instructions and Sw.\n	-- However, since the immediate mux is after the bypass mux,\n	-- it is unimportant when Rt is not a source. (e.g. addi, lw) \n	id_forwardB <= \"10\" when ((ex_regWrite = '1')	-- Valid Instruction producing Result at Stage Ex.\n		                  and (ex_rd = rt)			-- Ex target is our Rt source.\n		                  and (readsRt = '1')		-- This is not a Lui Instruction, Rt is read from.\n		                  and (rt /= empty)) else	-- Not reading $zero.\n				   \"01\" when ((mem_regWrite = '1')	-- Valid Instruction producing Result at Stage Mem.\n				   	      and (mem_rd = rt)			-- Mem Target is our Rt source.\n				   	      and (readsRt = '1')		-- This is not a Lui Instruction, Rt is read from.\n				   	      and (rt /= empty)) else	-- Not reading $zero.\n				   \"00\";\n	-- Forwarding Logic to Equality Comparator of Stage ID (Input A)\n	id_eqFwdA <= '1' when ((rs = mem_rd)              -- Mem Target is our Rs source.\n		               and (rs /= empty)              -- Not reading $zero.\n		               and (mem_isLoad = '0')         -- Not a Load, can't bypass with stall.\n		               and (mem_regWrite = '1')) else -- Valid Instruction producing Result at Stage Mem.\n		         '0';\n	-- Forwarding Logic to Equality Comparator of Stage ID (Input B)\n	id_eqFwdB <= '1' when ((rt = mem_rd)              -- Mem Target is our Rt source.\n		               and (rt /= empty)              -- Not reading $zero.\n		               and (mem_isLoad = '0')         -- Not a Load, can't bypass with stall.\n		               and (mem_regWrite = '1')) else -- Valid Instruction producing Result at Stage Mem.\n		         '0';\n	-- Forward just Loaded a value to a subsequent Store.\n	-- lw $t0, 0($s0)  # Load from s0 to t0.\n	-- sw $t0, 0($s1)  # Store from t0 to s1.\n	id_ldstBypass <= '1' when ((isStore = '1')     -- Store Word at Stage Id.\n		                   and (ex_isLoad = '1')   -- Load Word at Stage Ex.\n		                   and (ex_regWrite = '1') -- Valid Instruction producing Result at Stage Ex.\n		                   and (rt = ex_rd)        -- Store Word Register is the same one as the previous Load Word Register.\n		                   and (rt /= empty)) else -- Not reading $zero.\n		             '0';\n	stalling : process(rs, rt, isStore, isNop, readsRs, branch, ex_rd, ex_regWrite, ex_isLoad, mem_rd, mem_regWrite, mem_isLoad)\n	begin\n		ofStall <= '0'; -- Normally, no stalling happens.\n		-- -- Conservative Stalling. NO BYPASSING, except internally in register file.\n		-- Stalls for Data Dependence on Rs:\n--		if ((ex_regWrite = '1' and rs = ex_rd) or (mem_regWrite = '1' and rs = mem_rd)) and rs /= empty and readsRs = '1' and isNop = '0' then\n			-- Valid Instruction at Stage Ex and Reading the same Register, or\n			-- Valid Instruction at Stage Mem and Reading the same Register,\n			-- and the Register is not $zero, the Rs is actually read, and the Instruction is not Nop.\n--			ofStall <= '1';\n--		end if;\n		-- Stalls for Data Dependence on Rt:\n--		if ((ex_regWrite = '1' and rt = ex_rd) or (mem_regWrite = '1' and rt = mem_rd)) and rt /= empty and readsRt = '1' and isNop = '0' then\n			-- Valid Instruction at Stage Ex and Reading the same Register, or\n			-- Valid Instruction at Stage Mem and Reading the same Register,\n			-- and the Register is not $zero, the Rt is actually read, and the Instruction is not Nop.\n--			ofStall <= '1';\n--		end if;\n		-- Checking for Stalls from a Branch at Stage Id is for naught, as it is covered already.\n		-- If there is a dependence on an Instruction on Stage Wb, the value is forwarded\n		-- automatically inside the Register File, by writting itself on the same place.\n		-- -- Normal Stalling with Bypassing.\n		if branch = '1' and isNop = '0' then -- Branch Sources not ready. Beq too close to producer Rs or Rt.\n			if rs /= empty then -- Not reading $zero.\n				if rs = ex_rd and ex_regWrite = '1' then -- Rs comes from a previous Instruction.\n					ofStall <= '1';\n				elsif rs = mem_rd and mem_isLoad = '1' and mem_regWrite = '1' then 	-- Rs comes from two Instructions ago, which was a Load.\n					ofStall <= '1';													-- Instruction -3 is at Stage Wb, so it bypassed the new value through the Register File.\n				end if;\n			end if;\n			if rt /= empty then -- Not reading $zero.\n				if rt = ex_rd and ex_regWrite = '1' then -- Rt comes from a previous Instruction.\n					ofStall <= '1';\n				elsif rt = mem_rd and mem_isLoad = '1' and mem_regWrite = '1' then 	-- Rt comes from two Instructions ago, which was a Load.\n					ofStall <= '1';													-- Instruction -3 is at Stage Wb, so it bypassed the new value through the Register File.\n				end if;\n			end if;\n		-- Load-use Stall:\n	elsif ex_isLoad = '1' and ex_regWrite = '1' and rs = ex_rd and rs /= empty and readsRs = '1' and isNop = '0' then\n			-- Valid Load at Stage Ex, of the same Register, Rs not $zero, Rs is actually used, and it is not a Nop.\n			ofStall <= '1';\n		elsif ex_isLoad = '1' and ex_regWrite = '1' and rt = ex_rd and rt /= empty and readsRs = '1' and isNop = '0' and isStore = '0' then\n			-- Valid Load at Stage Ex, of the same Register, Rt not $zero, Rt is actually used, and it is not a Nop. Also, it is not a Store, which bypasses Rt.\n			ofStall <= '1';\n		end if;\n	end process stalling;\nend RTL;")) vhdl_entity_2: pin names not known; wires that end beside it: in_3[25:21], in_3[20:16], vhdl_entity_1_p7, vhdl_entity_1_p8, vhdl_entity_1_p3, vhdl_entity_1_p4, vhdl_entity_2_p7, in_5, in_6, in_7, in_8, in_10, in_12, out_28, out_29, out_30, out_20, out_21, vhdl_entity_2_p19, vhdl_entity_2_p20, out_23
  // VHDL_Entity #(.content("library ieee;\nuse ieee.std_logic_1164.all;\nuse ieee.numeric_std.all;\n\nentity regfile is\n	port(\n		clk : in  std_logic;\n		we3 : in  std_logic;\n		ra1 : in  std_logic_vector(4 downto 0);\n		ra2 : in  std_logic_vector(4 downto 0);\n		wa3 : in  std_logic_vector(4 downto 0);\n		wd3 : in  std_logic_vector(31 downto 0);\n		rd1 : out std_logic_vector(31 downto 0);\n		rd2 : out std_logic_vector(31 downto 0)\n	);\nend regfile;\n\narchitecture RTL of regfile is\n	type rfArray is array (31 downto 0) of std_logic_vector(31 downto 0);\n	signal rf      : rfArray := (others => (others => '0'));\n	constant empty : std_logic_vector(4 downto 0) := (others => '0');\nbegin\n	-- Three Ported Register File.\n	-- Read Ports ra1 and ra2 Combinationally.\n	-- Write Port wa3 on rising edge of the clock.\n	-- Register zero hardwired to $zero.\n	-- IMPORTANT: Bypasses stored value if Write Enabled, and (wa3 = ra1) or (wa3 = r2).\n	proc : process(clk)\n	begin\n		if (rising_edge(clk)) then\n			if (we3 = '1') then\n				rf(to_integer(unsigned(wa3))) <= wd3;\n			end if;\n		end if;\n	end process proc;\n	rd1 <= (others => '0') after 50 ns when (ra1 = empty)\n		else wd3 after 50 ns when ((we3 = '1') and (ra1 = wa3))\n		else rf(to_integer(unsigned(ra1))) after 50 ns;\n	rd2 <= (others => '0') after 50 ns when (ra2 = empty)\n		else wd3 after 50 ns when ((we3 = '1') and (ra2 = wa3))\n		else rf(to_integer(unsigned(ra2))) after 50 ns;\nend RTL;")) vhdl_entity_3: pin names not known; wires that end beside it: in_1, in_9, in_3[25:21], in_3[20:16], in_11, in_13, out_15, out_16
  Multiplexer #(.width(32), .enable("false")) multiplexer_3 (
    .in0({in_2[31:28], shifter_1_out}), .in1(adder_1_out), .out(out_14), .sel(vhdl_entity_1_p4));
  Multiplexer #(.width(32), .enable("false")) multiplexer_4 (
    .in0(out_15), .in1(in_4), .out(multiplexer_4_out), .sel(vhdl_entity_2_p19));
  Multiplexer #(.width(32), .enable("false")) multiplexer_5 (
    .in0(out_16), .in1(in_4), .out(multiplexer_5_out), .sel(vhdl_entity_2_p20));
  Comparator #(.width(32)) comparator_1 (
    .a(multiplexer_4_out), .b(multiplexer_5_out), .eq(comparator_1_eq));  // open: gt, lt
  not not_1 (not_1_out, out_30);
  and and_1 (vhdl_entity_2_p7, comparator_1_eq, vhdl_entity_1_p3);
  and and_2 (out_24, vhdl_entity_1_p11, not_1_out);
  and and_3 (out_27, vhdl_entity_1_p12, not_1_out);
endmodule

module IDEXpipe (
  input  in_1,
  input  [31:0] in_2,
  input  [31:0] in_3,
  input  [31:0] in_4,
  input  [2:0] in_5,
  input  in_6,
  input  [1:0] in_7,
  input  [1:0] in_8,
  input  in_9,
  input  in_10,
  input  in_11,
  input  in_12,
  input  [4:0] in_13,
  input  in_14,
  input  in_15,
  output [31:0] out_16,
  output [31:0] out_17,
  output [31:0] out_18,
  output [2:0] out_19,
  output out_20,
  output [1:0] out_21,
  output [1:0] out_22,
  output out_23,
  output out_24,
  output out_25,
  output out_26,
  output [4:0] out_27,
  output out_28
);

  Register #(.width(32)) rdA (.D(in_2), .en(1'b1), .clk(in_1), .Q(out_16), .clr(in_15));
  Register #(.width(32)) rdB (.D(in_3), .en(1'b1), .clk(in_1), .Q(out_17), .clr(in_15));
  Register #(.width(32)) imm (.D(in_4), .en(1'b1), .clk(in_1), .Q(out_18), .clr(in_15));
  Register #(.width(3)) alucont (.D(in_5), .en(1'b1), .clk(in_1), .Q(out_19), .clr(in_15));
  Register #(.width(1)) aluSrc (.D(in_6), .en(1'b1), .clk(in_1), .Q(out_20), .clr(in_15));
  Register #(.width(2)) forwardA (.D(in_7), .en(1'b1), .clk(in_1), .Q(out_21), .clr(in_15));
  Register #(.width(2)) forwardB (.D(in_8), .en(1'b1), .clk(in_1), .Q(out_22), .clr(in_15));
  Register #(.width(1)) isLoad (.D(in_9), .en(1'b1), .clk(in_1), .Q(out_23), .clr(in_15));
  Register #(.width(1)) ldstBypass (.D(in_10), .en(1'b1), .clk(in_1), .Q(out_24), .clr(in_15));
  Register #(.width(1)) memWrite (.D(in_11), .en(1'b1), .clk(in_1), .Q(out_25), .clr(in_15));
  Register #(.width(1)) memToReg (.D(in_12), .clk(in_1), .Q(out_26), .clr(in_15));  // open: en
  Register #(.width(5)) rd (.D(in_13), .en(1'b1), .clk(in_1), .Q(out_27), .clr(in_15));
  Register #(.width(1)) regWrite (.D(in_14), .en(1'b1), .clk(in_1), .Q(out_28), .clr(in_15));
endmodule

module ALU (
  input  [31:0] in_1,
  input  [31:0] in_2,
  input  [2:0] in_3,
  output [31:0] out_4
);

  wire [31:0] adder_1_out, and_1_out, bit_extender_1_out, multiplexer_1_out, or_1_out, xor_1_out;

  assign bit_extender_1_out = {{31{in_3[0]}}, in_3[0]};  // Bit_Extender bit_extender_1
  Adder #(.width(32)) adder_1 (.a(in_1), .b(xor_1_out), .out(adder_1_out));  // open: cin, cout
  assign xor_1_out = in_2 ^ bit_extender_1_out;  // XOR_Gate xor_1, 32 bits wide
  assign and_1_out = in_1 & in_2;  // AND_Gate and_1, 32 bits wide
  assign or_1_out = in_1 | in_2;  // OR_Gate or_1, 32 bits wide
  Multiplexer #(.width(32), .enable("false")) multiplexer_1 (
    .in0(and_1_out), .in1(or_1_out), .out(multiplexer_1_out), .sel(in_3[0]));
  Multiplexer #(.width(32), .enable("false")) multiplexer_2 (
    .in0(multiplexer_1_out), .in1(adder_1_out), .out(out_4), .sel(in_3[1]));
endmodule

module EXstage (
  input  [31:0] in_1,
  input  [31:0] in_2,
  input  [31:0] in_3,
  input  [2:0] in_4,
  input  in_5,
  input  [1:0] in_6,
  input  [1:0] in_7,
  input  in_8,
  input  in_9,
  input  in_10,
  input  in_11,
  input  [4:0] in_12,
  input  in_13,
  input  [31:0] in_14,
  input  [31:0] in_15,
  output [31:0] out_16,
  output [31:0] out_17,
  output out_18,
  output out_19,
  output out_20,
  output out_21,
  output [4:0] out_22,
  output out_23
);

  wire [31:0] multiplexer_1_out, vhdl_entity_1_p2;

  Multiplexer #(.select(2), .width(32), .enable("false")) multiplexer_1 (
    .in0(in_1), .in1(in_14), .in2(in_15), .out(multiplexer_1_out), .sel(in_6));  // open: in3
  Multiplexer #(.select(2), .width(32), .enable("false")) multiplexer_2 (
    .in0(in_2), .in1(in_14), .in2(in_15), .out(out_17), .sel(in_7));  // open: in3
  // VHDL_Entity #(.content("library ieee;\nuse ieee.std_logic_1164.all;\nuse ieee.numeric_std.all;\n\nentity alu is\n	port(\n		a       : in  std_logic_vector(31 downto 0);\n		b       : in  std_logic_vector(31 downto 0);\n		alucont : in  std_logic_vector(2 downto 0);\n--		zero    : out std_logic;\n		result  : out std_logic_vector(31 downto 0)\n	);\nend alu;\n\narchitecture RTL of alu is\n	signal b2  : std_logic_vector(31 downto 0);\n	signal sum : std_logic_vector(31 downto 0);\n	signal slt : std_logic_vector(31 downto 0);\n--	signal res : std_logic_vector(31 downto 0);\n	constant empty : std_logic_vector(30 downto 0) := (others => '0');\n--	constant empty32 : std_logic_vector(31 downto 0) := (others => '0');\nbegin\n	b2     <= not b when (alucont(2) = '1') else b;\n	sum    <= std_logic_vector(unsigned(a) + unsigned(b2) + unsigned(alucont(2 downto 2)));\n	slt    <= empty & sum(31);\n	with alucont(1 downto 0) select result <= -- Has to become \"res\" to be read for \"zero\".\n		a and b after 50 ns when \"00\",\n		 a or b after 50 ns when \"01\",\n		    sum after 50 ns when \"10\",\n		    slt after 50 ns when \"11\",\n		    (others => 'X') when others;\n--	zero   <= '1' when (res = empty32) else '0';\n--	result <= res;\nend RTL;")) vhdl_entity_1: pin names not known; wires that end beside it: multiplexer_1_out, vhdl_entity_1_p2, in_4, out_16
  Multiplexer #(.width(32), .enable("false")) multiplexer_3 (
    .in0(out_17), .in1(in_3), .out(vhdl_entity_1_p2), .sel(in_5));

  assign out_18 = in_8;
  assign out_19 = in_9;
  assign out_20 = in_10;
  assign out_21 = in_11;
  assign out_22 = in_12;
  assign out_23 = in_13;
endmodule

module EXMEMpipe (
  input  in_1,
  input  [31:0] in_2,
  input  [31:0] in_3,
  input  in_4,
  input  in_5,
  input  in_6,
  input  in_7,
  input  [4:0] in_8,
  input  in_9,
  input  in_10,
  output [31:0] out_11,
  output [31:0] out_12,
  output out_13,
  output out_14,
  output out_15,
  output out_16,
  output [4:0] out_17,
  output out_18
);

  Register #(.width(32)) register_1 (.D(in_2), .en(1'b1), .clk(in_1), .Q(out_11), .clr(in_10));
  Register #(.width(32)) register_2 (.D(in_3), .en(1'b1), .clk(in_1), .Q(out_12), .clr(in_10));
  Register #(.width(1)) register_3 (.D(in_4), .en(1'b1), .clk(in_1), .Q(out_13), .clr(in_10));
  Register #(.width(1)) register_4 (.D(in_5), .en(1'b1), .clk(in_1), .Q(out_14), .clr(in_10));
  Register #(.width(1)) register_5 (.D(in_6), .en(1'b1), .clk(in_1), .Q(out_15), .clr(in_10));
  Register #(.width(1)) register_6 (.D(in_7), .en(1'b1), .clk(in_1), .Q(out_16), .clr(in_10));
  Register #(.width(5)) register_7 (.D(in_8), .en(1'b1), .clk(in_1), .Q(out_17), .clr(in_10));
  Register #(.width(1)) register_8 (.D(in_9), .en(1'b1), .clk(in_1), .Q(out_18), .clr(in_10));
endmodule

module MEMstage (
  input  in_1,
  input  [31:0] in_2,
  input  [31:0] in_3,
  input  in_4,
  input  in_5,
  input  in_6,
  input  in_7,
  input  [4:0] in_8,
  input  in_9,
  input  [31:0] in_10,
  output [31:0] out_11,
  output [31:0] out_12,
  output out_13,
  output out_14,
  output [4:0] out_15,
  output out_16
);

  wire [31:0] multiplexer_1_out;

  Multiplexer #(.width(32), .enable("false")) multiplexer_1 (
    .in0(in_3), .in1(in_10), .out(multiplexer_1_out), .sel(in_5));
  // VHDL_Entity #(.content("library ieee;\nuse ieee.std_logic_1164.all;\nuse ieee.std_logic_textio.all;\nuse ieee.numeric_std.all;\nuse std.textio.all;\n\nentity dmem is\n	port(\n		clk : in  std_logic;\n		we  : in  std_logic;\n		a   : in  std_logic_vector(31 downto 0);\n		wd  : in  std_logic_vector(31 downto 0);\n		rd  : out std_logic_vector(31 downto 0)\n	);\nend dmem;\n\narchitecture RTL of dmem is\n	type memoryArray is array (63 downto 0) of std_logic_vector(31 downto 0);\n	impure function init_ram return memoryArray is\n		file inputText     : text;\n		variable inputLine : line;\n		variable temporal  : std_logic_vector(31 downto 0);\n		variable ram       : memoryArray := (others => (others => '0'));\n	begin\n		file_open(inputText, \"data_memfile.dat\", read_mode);\n		for index in 0 to 127 loop\n			if (endfile(inputText)) then\n				exit;\n			else\n				readline(inputText, inputLine);\n				hread(inputLine, temporal);\n				ram(index) := temporal;\n			end if;\n		end loop;\n		file_close(inputText);\n		return ram;\n	end init_ram;\n	signal ram : memoryArray := init_ram;\nbegin\n	proc : process(clk)\n	begin\n		if (rising_edge(clk)) then\n			if (we = '1') then\n				ram(to_integer(unsigned(a(7 downto 2)))) <= wd;\n			end if;\n		end if;\n	end process proc;\n	rd <= ram(to_integer(unsigned(a(7 downto 2)))) after 50 ns;\nend RTL;")) vhdl_entity_1: pin names not known; wires that end beside it: in_1, in_6, in_2, multiplexer_1_out, out_12

  assign out_11 = in_2;
  assign out_13 = in_4;
  assign out_14 = in_7;
  assign out_15 = in_8;
  assign out_16 = in_9;
endmodule

module MEMWBpipe (
  input  in_1,
  input  [31:0] in_2,
  input  [31:0] in_3,
  input  in_4,
  input  [4:0] in_5,
  input  in_6,
  input  in_7,
  output [31:0] out_8,
  output [31:0] out_9,
  output out_10,
  output [4:0] out_11,
  output out_12
);

  Register #(.width(32)) register_1 (.D(in_2), .en(1'b1), .clk(in_1), .Q(out_8), .clr(in_7));
  Register #(.width(32)) register_2 (.D(in_3), .en(1'b1), .clk(in_1), .Q(out_9), .clr(in_7));
  Register #(.width(1)) register_3 (.D(in_4), .en(1'b1), .clk(in_1), .Q(out_10), .clr(in_7));
  Register #(.width(5)) register_4 (.D(in_5), .en(1'b1), .clk(in_1), .Q(out_11), .clr(in_7));
  Register #(.width(1)) register_5 (.D(in_6), .en(1'b1), .clk(in_1), .Q(out_12), .clr(in_7));
endmodule

module WBstage (
  input  [31:0] in_1,
  input  [31:0] in_2,
  input  in_3,
  input  [4:0] in_4,
  input  in_5,
  output [31:0] out_6,
  output [4:0] out_7,
  output out_8
);

  Multiplexer #(.width(32), .enable("false")) multiplexer_1 (.in0(in_1), .in1(in_2), .out(out_6), .sel(in_3));

  assign out_7 = in_4;
  assign out_8 = in_5;
endmodule

module RISC (
);

  wire clock_1_out, exmempipe_1_out_13, exmempipe_1_out_14, exmempipe_1_out_15, exmempipe_1_out_16,
       exmempipe_1_out_18, exstage_1_out_18, exstage_1_out_19, exstage_1_out_20, exstage_1_out_21,
       exstage_1_out_23, idexpipe_1_out_20, idexpipe_1_out_23, idexpipe_1_out_24, idexpipe_1_out_25,
       idexpipe_1_out_26, idexpipe_1_out_28, idstage_1_out_19, idstage_1_out_22, idstage_1_out_23,
       idstage_1_out_24, idstage_1_out_25, idstage_1_out_27, idstage_1_out_28, idstage_1_out_29,
       idstage_1_out_30, memstage_1_out_13, memstage_1_out_14, memstage_1_out_16, memwbpipe_1_out_10,
       memwbpipe_1_out_12, por_1_out, wbstage_1_out_8;
  wire [1:0] idexpipe_1_out_21, idexpipe_1_out_22, idstage_1_out_20, idstage_1_out_21;
  wire [2:0] idexpipe_1_out_19, idstage_1_out_18;
  wire [4:0] exmempipe_1_out_17, exstage_1_out_22, idexpipe_1_out_27, idstage_1_out_26, memstage_1_out_15,
       memwbpipe_1_out_11, wbstage_1_out_7;
  wire [31:0] exmempipe_1_out_11, exmempipe_1_out_12, exstage_1_out_16, exstage_1_out_17, idexpipe_1_out_16,
       idexpipe_1_out_17, idexpipe_1_out_18, idstage_1_out_14, idstage_1_out_15, idstage_1_out_16,
       idstage_1_out_17, ifidpipe_1_out_6, ifidpipe_1_out_7, ifstage_1_out_7, ifstage_1_out_8,
       memstage_1_out_11, memstage_1_out_12, memwbpipe_1_out_8, memwbpipe_1_out_9, wbstage_1_out_6;

  Clock clock_1 (.out(clock_1_out));
  POR #(.PorHighDuration(1)) por_1 (.out(por_1_out));
  IFstage ifstage_1 (
    .out_8(ifstage_1_out_8), .in_5(idstage_1_out_30), .in_2(idstage_1_out_14), .out_7(ifstage_1_out_7),
    .in_1(clock_1_out), .in_6(por_1_out), .in_4(idstage_1_out_28), .in_3(idstage_1_out_29));
  IFIDpipe ifidpipe_1 (
    .in_5(por_1_out), .out_7(ifidpipe_1_out_7), .out_6(ifidpipe_1_out_6), .in_2(ifstage_1_out_7),
    .in_3(ifstage_1_out_8), .in_1(clock_1_out), .in_4(idstage_1_out_30));
  IDstage idstage_1 (
    .out_16(idstage_1_out_16), .in_8(memstage_1_out_15), .out_30(idstage_1_out_30),
    .out_27(idstage_1_out_27), .out_23(idstage_1_out_23), .in_9(wbstage_1_out_8), .out_17(idstage_1_out_17),
    .out_19(idstage_1_out_19), .in_11(wbstage_1_out_7), .in_2(ifidpipe_1_out_6), .out_26(idstage_1_out_26),
    .out_29(idstage_1_out_29), .in_6(idexpipe_1_out_28), .out_14(idstage_1_out_14),
    .out_22(idstage_1_out_22), .out_18(idstage_1_out_18), .in_10(memstage_1_out_16), .in_1(clock_1_out),
    .in_4(exmempipe_1_out_11), .out_24(idstage_1_out_24), .in_7(idexpipe_1_out_23),
    .out_15(idstage_1_out_15), .out_21(idstage_1_out_21), .in_13(wbstage_1_out_6), .in_5(idexpipe_1_out_27),
    .out_25(idstage_1_out_25), .out_28(idstage_1_out_28), .in_3(ifidpipe_1_out_7), .in_12(memstage_1_out_13),
    .out_20(idstage_1_out_20));
  IDEXpipe idexpipe_1 (
    .out_21(idexpipe_1_out_21), .in_9(idstage_1_out_22), .out_26(idexpipe_1_out_26),
    .out_22(idexpipe_1_out_22), .in_5(idstage_1_out_18), .in_3(idstage_1_out_16), .in_4(idstage_1_out_17),
    .in_13(idstage_1_out_26), .out_18(idexpipe_1_out_18), .out_25(idexpipe_1_out_25),
    .in_14(idstage_1_out_27), .out_17(idexpipe_1_out_17), .in_8(idstage_1_out_21), .in_7(idstage_1_out_20),
    .in_1(clock_1_out), .out_27(idexpipe_1_out_27), .out_23(idexpipe_1_out_23), .in_2(idstage_1_out_15),
    .in_11(idstage_1_out_24), .out_20(idexpipe_1_out_20), .in_12(idstage_1_out_25),
    .out_19(idexpipe_1_out_19), .in_10(idstage_1_out_23), .out_24(idexpipe_1_out_24),
    .out_28(idexpipe_1_out_28), .in_6(idstage_1_out_19), .in_15(por_1_out), .out_16(idexpipe_1_out_16));
  EXstage exstage_1 (
    .out_16(exstage_1_out_16), .in_8(idexpipe_1_out_23), .out_23(exstage_1_out_23),
    .out_19(exstage_1_out_19), .in_5(idexpipe_1_out_20), .in_13(idexpipe_1_out_28),
    .in_15(exmempipe_1_out_11), .in_7(idexpipe_1_out_22), .out_18(exstage_1_out_18),
    .out_22(exstage_1_out_22), .in_6(idexpipe_1_out_21), .in_10(idexpipe_1_out_25), .in_2(idexpipe_1_out_17),
    .out_20(exstage_1_out_20), .in_3(idexpipe_1_out_18), .in_11(idexpipe_1_out_26),
    .out_17(exstage_1_out_17), .in_9(idexpipe_1_out_24), .in_1(idexpipe_1_out_16), .out_21(exstage_1_out_21),
    .in_4(idexpipe_1_out_19), .in_12(idexpipe_1_out_27));  // open: in_14
  EXMEMpipe exmempipe_1 (
    .in_7(exstage_1_out_21), .out_15(exmempipe_1_out_15), .in_6(exstage_1_out_20), .in_8(exstage_1_out_22),
    .out_14(exmempipe_1_out_14), .out_18(exmempipe_1_out_18), .in_5(exstage_1_out_19),
    .out_13(exmempipe_1_out_13), .in_9(exstage_1_out_23), .in_1(clock_1_out), .out_16(exmempipe_1_out_16),
    .in_4(exstage_1_out_18), .out_12(exmempipe_1_out_12), .in_10(por_1_out), .in_2(exstage_1_out_16),
    .out_17(exmempipe_1_out_17), .in_3(exstage_1_out_17), .out_11(exmempipe_1_out_11));
  MEMstage memstage_1 (
    .in_7(exmempipe_1_out_16), .out_13(memstage_1_out_13), .in_4(exmempipe_1_out_13),
    .out_12(memstage_1_out_12), .in_6(exmempipe_1_out_15), .out_16(memstage_1_out_16),
    .in_5(exmempipe_1_out_14), .out_14(memstage_1_out_14), .in_9(exmempipe_1_out_18), .in_1(clock_1_out),
    .in_2(exmempipe_1_out_11), .in_10(wbstage_1_out_6), .in_8(exmempipe_1_out_17),
    .out_15(memstage_1_out_15), .in_3(exmempipe_1_out_12), .out_11(memstage_1_out_11));
  MEMWBpipe memwbpipe_1 (
    .in_7(por_1_out), .out_10(memwbpipe_1_out_10), .out_8(memwbpipe_1_out_8), .in_2(memstage_1_out_11),
    .in_1(clock_1_out), .out_9(memwbpipe_1_out_9), .in_5(memstage_1_out_15), .out_11(memwbpipe_1_out_11),
    .in_6(memstage_1_out_16), .in_4(memstage_1_out_14), .out_12(memwbpipe_1_out_12), .in_3(memstage_1_out_12));
  WBstage wbstage_1 (
    .out_8(wbstage_1_out_8), .out_7(wbstage_1_out_7), .in_1(memwbpipe_1_out_8), .out_6(wbstage_1_out_6),
    .in_2(memwbpipe_1_out_9), .in_5(memwbpipe_1_out_12), .in_3(memwbpipe_1_out_10), .in_4(memwbpipe_1_out_11));
endmodule
